// Logisim project addrdec.circ as structural Verilog: 1 circuit, main circuit main
module main (
  input  CLK,
  input  A15,
  input  A14,
  input  A13,
  input  A12,
  input  A11,
  input  A10,
  input  A9,
  input  A8,
  output RAM0,
  output RAM1,
  output VIA,
  output IRQ,
  output ACIA,
  output LCD,
  output DEV4,
  output DEV5,
  output DEV6,
  output DEV7,
  output ROM
);

  wire and_1_out, decoder_1_out0, decoder_1_out1, decoder_1_out2, decoder_1_out3, decoder_1_out4,
       decoder_1_out5, decoder_1_out6, decoder_1_out7, nand_1_out, nor_1_out, nor_2_out, nor_3_out,
       not_1_out, not_3_out, not_7_out;

  nand nand_1 (nand_1_out, A15, A14);
  nor nor_1 (nor_1_out, A13, A12, A11);
  not not_1 (not_1_out, A15);
  and and_1 (and_1_out, ~nand_1_out, nor_1_out);  // AND_Gate
  Decoder #(.select(3)) decoder_1 (
    .out0(decoder_1_out0), .out1(decoder_1_out1), .out2(decoder_1_out2), .out3(decoder_1_out3),
    .out4(decoder_1_out4), .out5(decoder_1_out5), .out6(decoder_1_out6), .out7(decoder_1_out7),
    .sel({A10, A9, A8}), .en(and_1_out));
  nor nor_2 (nor_2_out, nand_1_out, nor_1_out, 1'b0);
  not not_2 (ROM, nor_2_out);
  nand nand_2 (RAM0, not_1_out, CLK);
  nor nor_3 (nor_3_out, not_1_out, A14);
  not not_3 (not_3_out, CLK);
  not not_4 (VIA, decoder_1_out0);
  not not_5 (IRQ, decoder_1_out1);
  not not_6 (ACIA, decoder_1_out2);
  not not_7 (not_7_out, decoder_1_out3);
  not not_8 (DEV4, decoder_1_out4);
  not not_9 (DEV5, decoder_1_out5);
  not not_10 (DEV6, decoder_1_out6);
  not not_11 (DEV7, decoder_1_out7);
  nand nand_3 (RAM1, nor_3_out, CLK);
  nor nor_4 (LCD, not_3_out, 1'b0, not_7_out);
endmodule
