// Logisim project rw_split.circ as structural Verilog: 1 circuit, main circuit main
module main (
  input  in_1
);

  wire clock_1_out, nand_1_out, nand_2_out, nand_3_out;

  nand nand_1 (nand_1_out, in_1, in_1);
  Clock clock_1 (.out(clock_1_out));
  nand nand_2 (nand_2_out, nand_1_out, clock_1_out);
  LED #(.active("false")) led_1 (.in(nand_2_out));
  nand nand_3 (nand_3_out, clock_1_out, in_1);
  LED #(.active("false")) led_2 (.in(nand_3_out));
endmodule
