// Logisim project irq_rw.circ as structural Verilog: 1 circuit, main circuit main
module main (
  input  CS,
  input  RW,
  output W,
  output R
);

  wire nor_1_out, not_2_out;

  nor nor_1 (nor_1_out, CS, RW);
  not not_1 (W, nor_1_out);
  not not_2 (not_2_out, CS);
  nand nand_1 (R, not_2_out, RW);
endmodule
